# Fritzing sketch rpi_1b_dht (saved by Fritzing 0.9.3b)

parts:
  Raspberry_Pi_B_rev1 = Raspberry Pi B rev1
  DHT1 = DHT22 Humidity and Temperature Sensor [part_number=DHT21]
  DHT2 = DHT22 Humidity and Temperature Sensor [part_number=DHT21]  # not connected

nets:
  3V3: Raspberry_Pi_B_rev1.3V3, DHT1.VDD
